// Logisim project new_processor.circ as structural Verilog: 14 circuits, main circuit main
module main (
);

  wire alu_1_lt, alu_1_ltu, control_unit_1_alusrc, control_unit_1_memtoreg, control_unit_1_rw,
       control_unit_1_su, control_unit_1_wos, or_1_out, register_file_1_p5, register_file_1_p6, undriven,
       undriven_2;
  wire [1:0] control_unit_1_whb;
  wire [3:0] control_unit_1_alu_operator;
  wire [4:0] split_out_2, split_out_3, split_out_4;
  wire [11:0] split_out_5;
  wire [31:0] adder_1_out, alu_1_result, data_memory_1_read_data, immediate_generator_1_immediate_out,
       instruction_memory_1_instruction, multiplexer_1_out, multiplexer_2_out, multiplexer_5_out,
       multiplexer_6_out, pc_1_nextaddress, register_file_1_p4, register_file_1_p7,
       sign_zero_extention_1_write_data_ext, store_word_halfword_byte_1_data_out;

  PC pc_1 (.PreviousAddress(adder_1_out), .NextAddress(pc_1_nextaddress));
  Adder #(.width(32)) adder_1 (.a(32'h4), .b(pc_1_nextaddress), .out(adder_1_out));  // open: cin, cout
  Instruction_Memory instruction_memory_1 (
    .Address(pc_1_nextaddress), .Instruction(instruction_memory_1_instruction));  // open: clk, rst
  instr_split split (
    .instr(instruction_memory_1_instruction), .out_2(split_out_2), .out_3(split_out_3), .out_4(split_out_4),
    .out_5(split_out_5));
  // Register_File register_file_1: pin names not known; wires that end beside it: split_out_2, split_out_3, split_out_4, register_file_1_p4, register_file_1_p5, register_file_1_p6, register_file_1_p7
  Immediate_Generator immediate_generator_1 (
    .Immediate_In(split_out_5), .Immediate_Out(immediate_generator_1_immediate_out));
  Control_Unit control_unit_1 (
    .Instruction(instruction_memory_1_instruction), .RegWrite(register_file_1_p5), .rw(control_unit_1_rw),
    .MemtoReg(control_unit_1_memtoreg), .ALUSrc(control_unit_1_alusrc), .su(control_unit_1_su),
    .wos(control_unit_1_wos), .alu_operator(control_unit_1_alu_operator), .whb(control_unit_1_whb));
  Multiplexer multiplexer_1 (
    .in0(pc_1_nextaddress[0]), .in1(register_file_1_p6), .out(multiplexer_1_out[0]));  // open: sel
  Multiplexer #(.width(32)) multiplexer_2 (
    .in0(register_file_1_p7), .in1(immediate_generator_1_immediate_out), .out(multiplexer_2_out),
    .sel(control_unit_1_alusrc));
  shift_by_1 shift_by_1_1 (.\input (immediate_generator_1_immediate_out));
  ALU alu_1 (
    .A(multiplexer_1_out), .B(multiplexer_2_out), .ALU_Operator(control_unit_1_alu_operator),
    .Result(alu_1_result), .lt(alu_1_lt), .ltu(alu_1_ltu));  // open: zero
  Store_Word_HalfWord_Byte store_word_halfword_byte_1 (
    .Data_In(register_file_1_p7), .whb(control_unit_1_whb), .Data_Out(store_word_halfword_byte_1_data_out));
  Multiplexer multiplexer_3 (.in0(adder_1_out[0]), .in1(undriven), .out(adder_1_out[0]), .sel(undriven_2));
  Multiplexer #(.width(32)) multiplexer_4 (
    .in0(multiplexer_5_out), .in1(sign_zero_extention_1_write_data_ext), .out(register_file_1_p4),
    .sel(control_unit_1_wos));
  or or_1 (or_1_out, alu_1_ltu, alu_1_lt);
  Multiplexer #(.width(32)) multiplexer_5 (.in0({32{1'b0}}), .in1(32'h1), .out(multiplexer_5_out), .sel(or_1_out));
  Data_Memory data_memory_1 (
    .Addreses(alu_1_result), .Write_Data(store_word_halfword_byte_1_data_out), .rw(control_unit_1_rw),
    .Read_Data(data_memory_1_read_data));  // open: clk, rst
  Multiplexer #(.width(32)) multiplexer_6 (
    .in0(alu_1_result), .in1(data_memory_1_read_data), .out(multiplexer_6_out), .sel(control_unit_1_memtoreg));
  Sign_Zero_Extention sign_zero_extention_1 (
    .Write_Data(multiplexer_6_out), .whb(control_unit_1_whb), .su(control_unit_1_su),
    .Write_Data_Ext(sign_zero_extention_1_write_data_ext));
  // Pins of 1 and 32 bits meet at pc_1_nextaddress
  // Pins of 1 and 32 bits meet at multiplexer_1_out
  // Pins of 1 and 32 bits meet at adder_1_out

  // Notes on the sheet:
  //         PC_src
endmodule

module Instruction_Memory (
  input  [31:0] Address,
  input  clk,
  input  rst,
  output [31:0] Instruction
);
endmodule

module Register_File (
  input  [4:0] rs1,
  input  [4:0] rs2,
  input  [4:0] rd,
  input  [31:0] WriteData,
  input  clk,
  input  rst,
  input  RegWrite,
  output [31:0] ReadData1,
  output [31:0] ReadData2
);
endmodule

module Immediate_Generator (
  input  [11:0] Immediate_In,
  output [31:0] Immediate_Out
);
endmodule

module Store_Word_HalfWord_Byte (
  input  [31:0] Data_In,
  input  [1:0] whb,
  output [31:0] Data_Out
);
endmodule

module ALU (
  input  [31:0] A,
  input  [31:0] B,
  input  [3:0] ALU_Operator,
  output zero,
  output [31:0] Result,
  output lt,
  output ltu
);
endmodule

module Data_Memory (
  input  [31:0] Addreses,
  input  [31:0] Write_Data,
  input  rw,
  input  clk,
  input  rst,
  output [31:0] Read_Data
);
endmodule

module Sign_Zero_Extention (
  input  [31:0] Write_Data,
  input  [1:0] whb,
  input  su,
  output [31:0] Write_Data_Ext
);
endmodule

module PC (
  input  [31:0] PreviousAddress,
  output [31:0] NextAddress
);
endmodule

module instr_split (
  input  [31:0] instr,
  output [4:0] out_2,
  output [4:0] out_3,
  output [4:0] out_4,
  output [11:0] out_5
);
endmodule

module Control_Unit (
  input  [31:0] Instruction,
  output RegWrite,
  output rw,
  output MemtoReg,
  output ALUSrc,
  output su,
  output wos,
  output [3:0] alu_operator,
  output [1:0] whb
);
endmodule

module shift_by_1 (
  input  [31:0] \input 
);


  // Notes on the sheet:
  //   output
endmodule

module pc_src (
  input  in_1,
  input  in_2,
  input  in_3,
  input  zero,
  input  lt,
  input  BEQ,
  input  jump,
  input  ltu,
  input  BLT,
  input  in_10,
  input  BEG,
  input  BLTU,
  input  BEGU
);

  wire and_1_out, controlled_buffer_1_out, not_1_out, not_2_out, or_1_out, or_2_out, or_3_out;

  or or_1 (or_1_out, in_1, in_2);
  not not_1 (not_1_out, lt);
  not not_2 (not_2_out, ltu);
  or or_2 (or_2_out, not_1_out, zero);
  or or_3 (or_3_out, not_2_out, zero);
  and and_1 (and_1_out, in_3, zero);
  and and_2 (and_1_out, BEQ, zero);
  buf and_3 (and_1_out, lt);  // AND_Gate
  and and_4 (and_1_out, BEG, or_2_out);
  and and_5 (and_1_out, BLTU, ltu);
  and and_6 (and_1_out, BEGU, or_3_out);
  assign controlled_buffer_1_out = jump ? or_1_out : 1'bz;  // Controlled_Buffer controlled_buffer_1
  assign controlled_buffer_1_out = in_10 ? and_1_out : 1'bz;  // Controlled_Buffer controlled_buffer_2

  // Notes on the sheet:
  //   BNE
  //   branch
  //   PC_src
endmodule

module pc_jump (
);

  wire [1:0] undriven;
  wire [31:0] adder_1_out, immediate_generator_1_immediate_out, multiplexer_1_out, pc_1_nextaddress;

  PC pc_1 (.PreviousAddress(multiplexer_1_out), .NextAddress(pc_1_nextaddress));
  Adder #(.width(32)) adder_1 (.a(32'h4), .b(pc_1_nextaddress), .out(adder_1_out));  // open: cin, cout
  Immediate_Generator immediate_generator_1 (.Immediate_Out(immediate_generator_1_immediate_out));  // open: Immediate_In
  shift_by_1 shift_by_1_1 (.\input (immediate_generator_1_immediate_out));
  Multiplexer #(.width(2)) multiplexer_1 (
    .in0(adder_1_out[1:0]), .in1(undriven), .out(multiplexer_1_out[1:0]));  // open: sel
  // Pins of 2 and 32 bits meet at adder_1_out
  // Pins of 2 and 32 bits meet at multiplexer_1_out

  // Notes on the sheet:
  //   pc_src
endmodule
